# Fritzing sketch Accelerometer (saved by Fritzing 0.9.2b)
breadboards: 1

parts:
  Part1 = Arduino Uno (Rev3)
  Part2 = Triple Axis Accelerometer Breakout - ADXL335

nets:
  N1: Part1.A0, Part2.XOUT
  N2: Part1.A1, Part2.YOUT
  N3: Part1.A2, Part2.ZOUT
  3V3: Part1.3V3, Part2.VCC
  GND: Part1.GND, Part2.GND

notes:
  Sparkfun ADXL335 Accelerometer
