# Fritzing sketch Digital_Input_Output (saved by Fritzing 0.9.2b)
breadboards: 1

parts:
  Part1 = Arduino Uno (Rev3)
  R1 = Resistor [tolerance=±5% resistance=220 package=THT]
  S1 = Square Pushbutton
  R2 = Resistor [tolerance=±5% resistance=100 package=THT]
  LED1 = smd LED [color="Red (633nm)" package="0805 [SMD]"]

nets:
  N1: Part1.D12/MISO, LED1.anode
  N2: Part1.D2, R1.Pin_1, S1.leg0
  N3: Part1.5V, S1.leg1
  N4: Part1.GND, R1.Pin_0, R2.Pin_0
  N5: R2.Pin_1, LED1.cathode

// code stored in the sketch: BasicInputOutput.ino
int LED = 12;
int toggle = 2;
void setup() {
  // put your setup code here, to run once:
  pinMode(LED, OUTPUT);
  pinMode(toggle, INPUT);
  Serial.begin(9600);
  
}

void loop() {
  // put your main code here, to run repeatedly:
Serial.println(digitalRead(toggle));
digitalWrite(LED, digitalRead(toggle));
}
