# Fritzing sketch LCD_Screen_4Bit (saved by Fritzing 0.9.2b)
breadboards: 1

parts:
  Part1 = Arduino Uno (Rev3)
  U1 = LCD-16X2 [package=lcd-16x2_noholes]
  U2 = POT [package=alps_pot]

nets:
  N1: Part1.D11_PWM/MOSI, U1.E
  N2: Part1.D12/MISO, U1.RS
  GND: Part1.GND, U1.VSS, U1.R_W, U2.A
  N3: Part1.D2, U1.DB7
  N4: Part1.D3_PWM, U1.DB6
  N5: Part1.D4, U1.DB5
  N6: Part1.D5_PWM, U1.DB4
  5V: Part1.5V, U1.VDD, U1.A, U1.K, U2.E
  N7: U1.VO, U2.S

notes:
  10k Potentiometer controls backlight intensity
  JHD162A Backlit LCD
