# Fritzing sketch LEDsSwitchesConditionals (saved by Fritzing 0.9.2b)
breadboards: 1

parts:
  Part1 = Arduino Uno (Rev3)
  R1 = Resistor [tolerance=±5% resistance=220 package=THT]
  S1 = Square Pushbutton
  R2 = Resistor [tolerance=±5% resistance=100 package=THT]
  LED1 = smd LED [color="Red (633nm)" package="0805 [SMD]"]
  LED2 = smd LED [color="Red (633nm)" package="0805 [SMD]"]
  R3 = Resistor [tolerance=±5% resistance=100 package=THT]
  R4 = Resistor [tolerance=±5% resistance=220 package=THT]
  S2 = Square Pushbutton

nets:
  N1: Part1.D11_PWM/MOSI, LED2.anode
  N2: Part1.D12/MISO, LED1.anode
  N3: Part1.D2, R1.Pin_1, S1.leg0
  N4: Part1.D3_PWM, R4.Pin_1, S2.leg0
  N5: Part1.5V, S1.leg1, S2.leg1
  N6: Part1.GND, R1.Pin_0, R2.Pin_0, R3.Pin_0, R4.Pin_0
  N7: R2.Pin_1, LED1.cathode
  N8: LED2.cathode, R3.Pin_1

// code stored in the sketch: BasicInputOutput.ino
int led_1 = 11;
int led_2 = 12;

int toggle_1 = 2;
int toggle_2 = 3;

void setup() {
  // put your setup code here, to run once:
  pinMode(led_1, OUTPUT);
  pinMode(led_2, OUTPUT);

  pinMode(toggle_1, INPUT);
  pinMode(toggle_2, INPUT);
}

void loop() {
  // put your main code here, to run repeatedly:
  if(digitalRead(toggle_1) && digitalRead(toggle_2)){

    digitalWrite(led_1, HIGH);
    digitalWrite(led_2, HIGH);

    delay(500);

    digitalWrite(led_1, LOW);
    digitalWrite(led_2, LOW);
     
    delay(500);
  }else if(digitalRead(toggle_1)){

    digitalWrite(led_1, HIGH);
    digitalWrite(led_2, LOW);
  }else if(digitalRead(toggle_2)){

    digitalWrite(led_1, LOW);
    digitalWrite(led_2, HIGH);
  }else{

   digitalWrite(led_1, HIGH);
   digitalWrite(led_2, HIGH);
  }
}
