# Fritzing sketch PING_3Pin (saved by Fritzing 0.9.2b)
breadboards: 1

parts:
  Part1 = Arduino Uno (Rev3)
  R2 = Resistor [tolerance=±5% resistance=100 package=THT]
  LED1 = smd LED [color="Green (560nm)" package="0805 [SMD]"]
  J1 = Infrared Proximity Sensor

nets:
  N1: Part1.D12/MISO, LED1.anode
  N2: Part1.D7, J1.Vout
  5V: Part1.5V, J1.Vcc
  GND: Part1.GND, R2.Pin_0, J1.GND
  N3: R2.Pin_1, LED1.cathode

notes:
  Parallax PING))) Ultrasonic Distance Detector

// code stored in the sketch: BasicInputOutput.ino
int LED = 12;
int toggle = 2;
void setup() {
  // put your setup code here, to run once:
  pinMode(LED, OUTPUT);
  pinMode(toggle, INPUT);
  Serial.begin(9600);
  
}

void loop() {
  // put your main code here, to run repeatedly:
Serial.println(digitalRead(toggle));
digitalWrite(LED, digitalRead(toggle));
}
