# Fritzing sketch PIR (saved by Fritzing 0.9.2b)
breadboards: 1

parts:
  Part1 = Arduino Uno (Rev3)
  LED1 = LED - 3mm [color="Green (570nm)" package="3 mm [THT]"]
  LED2 = LED - 3mm [color="Red (633nm)" package="3 mm [THT]"]
  R1 = Resistor [tolerance=±5% resistance=220 package="0402 [SMD]"]
  R2 = Resistor [tolerance=±5% resistance=220 package="0402 [SMD]"]
  PIR1 = PIR sensor
  R3 = Resistor [tolerance=±5% resistance=10k package="0402 [SMD]"]

nets:
  N1: Part1.D8, LED1.anode
  GND: Part1.GND, R1.Pin_1, R2.Pin_1, PIR1.GND
  N2: Part1.D2, PIR1.SIG, R3.Pin_0
  N3: Part1.D7, LED2.anode
  5V: Part1.5V, PIR1.VDD, R3.Pin_1
  N4: LED1.cathode, R1.Pin_0
  N5: LED2.cathode, R2.Pin_0

notes:
  Sparkfun SEN-13285 PIR Motion Sensor
