# Fritzing sketch PhotoResistor (saved by Fritzing 0.9.2b)
breadboards: 1

parts:
  Part1 = Arduino Uno (Rev3)
  R1 = PHOTOCELL [package=photocell-kit]
  R2 = Resistor [tolerance=±5% resistance=220 package="1206 [SMD]"]

nets:
  N1: Part1.A0, R1.P$2, R2.Pin_1
  N2: Part1.5V, R2.Pin_0
  N3: Part1.GND, R1.P$1
