# Fritzing sketch Potentiometer_Servo_Control (saved by Fritzing 0.9.2b)
breadboards: 1

parts:
  Part1 = Arduino Uno (Rev3)
  J1 = Basic Servo
  R1 = Rotary Potentiometer (Small) [maximum_resistance=100kΩ package=THT]

nets:
  N1: Part1.A0, R1.wiper
  N2: Part1.D9_PWM, J1.pulse
  5V: Part1.5V, J1.vcc, R1.leg2
  GND: Part1.GND, J1.gnd, R1.leg1

// code stored in the sketch: BasicInputOutput.ino
int LED = 12;
int toggle = 2;
void setup() {
  // put your setup code here, to run once:
  pinMode(LED, OUTPUT);
  pinMode(toggle, INPUT);
  Serial.begin(9600);
  
}

void loop() {
  // put your main code here, to run repeatedly:
Serial.println(digitalRead(toggle));
digitalWrite(LED, digitalRead(toggle));
}
